// Logisim project RISC-V.circ as structural Verilog: 17 circuits, main circuit Datapath
module Datapath (
  output [31:0] out
);

  wire bsel, clk_t, controllogic_1_wbsel, regwena;
  wire [2:0] controllogic_1_lsel, immsel;
  wire [3:0] alusel;
  wire [7:0] bitselector_1_out, shifter_1_out;
  wire [31:0] aluctl_1_datab, dataD, immediategen_1_imm31_0, lw_t, register_1_rs1, register_1_rs2;

  Clock clock_1 (.out(clk_t));
  Register register_1 (
    .rsi1(5'b00011), .rsi2(5'b00100), .rdi(5'b00010), .rd(out), .we(regwena), .rs1(register_1_rs1),
    .rs2(register_1_rs2), .clk(clk_t));
  ImmediateGen immediategen_1 (.Ins(32'h418133), .sel(immsel), .imm31_0(immediategen_1_imm31_0));
  ControlLogic controllogic_1 (
    .Ins(32'h418133), .alusel(alusel), .regwena(regwena), .immsel(immsel), .bsel(bsel),
    .lsel(controllogic_1_lsel), .wbsel(controllogic_1_wbsel));
  BitSelector #(.width(32), .group(8)) bitselector_1 (.in(out), .out(bitselector_1_out), .sel(2'b00));
  ALUCTL aluctl_1 (.rs2(register_1_rs2), .imm31_0(immediategen_1_imm31_0), .bsel(bsel), .dataB(aluctl_1_datab));
  Shifter #(.shift("lr")) shifter_1 (.in(bitselector_1_out), .\dist (3'b010), .out(shifter_1_out));
  LoadCtl loadctl_1 (.A(out), .lw(lw_t), .lsel(controllogic_1_lsel), .wbsel(controllogic_1_wbsel), .out_5(dataD));
  RAM #(.dataWidth(32), .bus("separate")) ram_1 (
    .addr(shifter_1_out), .data(lw_t), .clk(clk_t));  // open: din, str, sel, ld, clr
  ALU alu_1 (.dataA(register_1_rs1), .dataB(aluctl_1_datab), .Sel(alusel), .dataD(out));

  // Other names for the same wires on the sheet: ALU_A[31:0] = out

  // Notes on the sheet:
  //   add x2, x3, x4
  //   sub x2, x3, x4
  //   or x2, x3, x4
  //   and x2, x3, x4
  //   xor x2, x3, x4 
  //   sll x2, x3, x4
  //   slt x2, x3, x4
  //   Ins
  //   0x00418133
  //   0x40418133
  //   0x0041e133
  //   0x0041f133
  //   0x0041c133
  //   0x00419133
  //   0x0041a133
  //   Use RISC Online Assembler to get more Machine Language Codes (Ins)
endmodule

module PC (
  input  clk,
  input  [31:0] inPC,
  output [31:0] outPC_4,
  output [31:0] outPC
);

  Register_part #(.width(32)) register_1 (.D(inPC), .en(1'b1), .Q(outPC), .clk(clk));  // open: clr
  Adder #(.width(32)) adder_1 (.a(outPC), .b(32'h4), .out(outPC_4));  // open: cin, cout

  // Other names for the same wires on the sheet: clk_t = clk; inPC_t[31:0] = inPC; outPC4_t[31:0] = outPC_4;
  //   outPC_t[31:0] = outPC
endmodule

module ControlLogic (
  input  [31:0] Ins,
  output [3:0] alusel,
  output regwena,
  output bsel,
  output [2:0] immsel,
  output wbsel,
  output [2:0] lsel
);

  wire lsel0_t, lsel1_t, lsel2_t;

  ROM #(.addrWidth(9), .dataWidth(13)) rom_1 (
    .addr({Ins[30], Ins[14:12], Ins[6:2]}),
    .data({lsel2_t, lsel1_t, lsel0_t, wbsel, alusel, regwena, immsel, bsel}));  // open: sel

  // Other names for the same wires on the sheet: i2_t = Ins[2]; i3_t = Ins[3]; i4_t = Ins[4]; i5_t = Ins[5];
  //   i6_t = Ins[6]; i12_t = Ins[12]; i13_t = Ins[13]; i14_t = Ins[14]; i30_t = Ins[30]; bsel_t = bsel;
  //   is0_t = immsel[0]; is1_t = immsel[1]; is2_t = immsel[2]; regwena_t = regwena; as0_t = alusel[0];
  //   as1_t = alusel[1]; as2_t = alusel[2]; as3_t = alusel[3]; wbsel_t = wbsel; isel0_t = lsel[0]; isel1_t = lsel[1];
  //   isel2_t = lsel[2]

  // Notes on the sheet:
  //   contents of rom_1 (hex, n*v repeats v):
  //   11 0 0 0 11 7*0 10 19*0 11 0 0 0 31 7*0 30 19*0 11 0 0 0 51 7*0 50 23*0 71 7*0 70 19*0 11 0 0 0 91
  //   7*0 90 19*0 11 0 0 0 b1 7*0 b0 23*0 d1 7*0 d0 23*0 f1 7*0 f0 31*0 110 151*0 1b1 7*0 1b0
endmodule

module Register (
  input  [4:0] rsi1,
  input  [4:0] rsi2,
  input  [4:0] rdi,
  input  [31:0] rd,
  input  we,
  input  clk,
  output [31:0] rs1,
  output [31:0] rs2
);

  wire r0we_t, r1we_t, r2we_t, r3we_t, r4we_t, r5we_t, r6we_t, r7we_t, r8we_t, r9we_t, r10we_t, r11we_t,
       r12we_t, r13we_t, r14we_t, r15we_t, r16we_t, r17we_t, r18we_t, r19we_t, r20we_t, r21we_t, r22we_t,
       r23we_t, r24we_t, r25we_t, r26we_t, r27we_t, r28we_t, r29we_t, r30we_t, r31we_t;
  wire [31:0] r1q_t, r2q_t, r3q_t, r4q_t, r5q_t, r6q_t, r7q_t, r8q_t, r9q_t, r10q_t, r11q_t, r12q_t, r13q_t,
       r14q_t, r15q_t, r16q_t, r17q_t, r18q_t, r19q_t, r20q_t, r21q_t, r22q_t, r23q_t, r24q_t, r25q_t,
       r26q_t, r27q_t, r28q_t, r29q_t, r30q_t, r31q_t;

  Multiplexer #(.select(5), .width(32)) multiplexer_1 (
    .in0({32{1'b0}}), .in1(r1q_t), .in2(r2q_t), .in3(r3q_t), .in4(r4q_t), .in5(r5q_t), .in6(r6q_t),
    .in7(r7q_t), .in8(r8q_t), .in9(r9q_t), .in10(r10q_t), .in11(r11q_t), .in12(r12q_t), .in13(r13q_t),
    .in14(r14q_t), .in15(r15q_t), .in16(r16q_t), .in17(r17q_t), .in18(r18q_t), .in19(r19q_t), .in20(r20q_t),
    .in21(r21q_t), .in22(r22q_t), .in23(r23q_t), .in24(r24q_t), .in25(r25q_t), .in26(r26q_t), .in27(r27q_t),
    .in28(r28q_t), .in29(r29q_t), .in30(r30q_t), .in31(r31q_t), .out(rs1), .sel(rsi1));  // open: en
  Multiplexer #(.select(5), .width(32)) multiplexer_2 (
    .in0({32{1'b0}}), .in1(r1q_t), .in2(r2q_t), .in3(r3q_t), .in4(r4q_t), .in5(r5q_t), .in6(r6q_t),
    .in7(r7q_t), .in8(r8q_t), .in9(r9q_t), .in10(r10q_t), .in11(r11q_t), .in12(r12q_t), .in13(r13q_t),
    .in14(r14q_t), .in15(r15q_t), .in16(r16q_t), .in17(r17q_t), .in18(r18q_t), .in19(r19q_t), .in20(r20q_t),
    .in21(r21q_t), .in22(r22q_t), .in23(r23q_t), .in24(r24q_t), .in25(r25q_t), .in26(r26q_t), .in27(r27q_t),
    .in28(r28q_t), .in29(r29q_t), .in30(r30q_t), .in31(r31q_t), .out(rs2), .sel(rsi2));  // open: en
  Demultiplexer #(.select(5)) demultiplexer_1 (
    .out0(r0we_t), .out1(r1we_t), .out2(r2we_t), .out3(r3we_t), .out4(r4we_t), .out5(r5we_t), .out6(r6we_t),
    .out7(r7we_t), .out8(r8we_t), .out9(r9we_t), .out10(r10we_t), .out11(r11we_t), .out12(r12we_t),
    .out13(r13we_t), .out14(r14we_t), .out15(r15we_t), .out16(r16we_t), .out17(r17we_t), .out18(r18we_t),
    .out19(r19we_t), .out20(r20we_t), .out21(r21we_t), .out22(r22we_t), .out23(r23we_t), .out24(r24we_t),
    .out25(r25we_t), .out26(r26we_t), .out27(r27we_t), .out28(r28we_t), .out29(r29we_t), .out30(r30we_t),
    .out31(r31we_t), .in(we), .sel(rdi));  // open: en
  Register_part #(.width(32)) x4 (.D(rd), .en(r4we_t), .Q(r4q_t), .clk(clk));  // open: clr
  Register_part #(.width(32)) x8 (.D(rd), .en(r8we_t), .Q(r8q_t), .clk(clk));  // open: clr
  Register_part #(.width(32)) x12 (.D(rd), .en(r12we_t), .Q(r12q_t), .clk(clk));  // open: clr
  Register_part #(.width(32)) x16 (.D(rd), .en(r16we_t), .Q(r16q_t), .clk(clk));  // open: clr
  Register_part #(.width(32)) x20 (.D(rd), .en(r20we_t), .Q(r20q_t), .clk(clk));  // open: clr
  Register_part #(.width(32)) x24 (.D(rd), .en(r24we_t), .Q(r24q_t), .clk(clk));  // open: clr
  Register_part #(.width(32)) x28 (.D(rd), .en(r28we_t), .Q(r28q_t), .clk(clk));  // open: clr
  Register_part #(.width(32)) x1 (.D(rd), .en(r1we_t), .Q(r1q_t), .clk(clk));  // open: clr
  Register_part #(.width(32)) x5 (.D(rd), .en(r5we_t), .Q(r5q_t), .clk(clk));  // open: clr
  Register_part #(.width(32)) x9 (.D(rd), .en(r9we_t), .Q(r9q_t), .clk(clk));  // open: clr
  Register_part #(.width(32)) x13 (.D(rd), .en(r13we_t), .Q(r13q_t), .clk(clk));  // open: clr
  Register_part #(.width(32)) x17 (.D(rd), .en(r17we_t), .Q(r17q_t), .clk(clk));  // open: clr
  Register_part #(.width(32)) x21 (.D(rd), .en(r21we_t), .Q(r21q_t), .clk(clk));  // open: clr
  Register_part #(.width(32)) x25 (.D(rd), .en(r25we_t), .Q(r25q_t), .clk(clk));  // open: clr
  Register_part #(.width(32)) x29 (.D(rd), .en(r29we_t), .Q(r29q_t), .clk(clk));  // open: clr
  Register_part #(.width(32)) x2 (.D(rd), .en(r2we_t), .Q(r2q_t), .clk(clk));  // open: clr
  Register_part #(.width(32)) x6 (.D(rd), .en(r6we_t), .Q(r6q_t), .clk(clk));  // open: clr
  Register_part #(.width(32)) x10 (.D(rd), .en(r10we_t), .Q(r10q_t), .clk(clk));  // open: clr
  Register_part #(.width(32)) x14 (.D(rd), .en(r14we_t), .Q(r14q_t), .clk(clk));  // open: clr
  Register_part #(.width(32)) x18 (.D(rd), .en(r18we_t), .Q(r18q_t), .clk(clk));  // open: clr
  Register_part #(.width(32)) x22 (.D(rd), .en(r22we_t), .Q(r22q_t), .clk(clk));  // open: clr
  Register_part #(.width(32)) x26 (.D(rd), .en(r26we_t), .Q(r26q_t), .clk(clk));  // open: clr
  Register_part #(.width(32)) x30 (.D(rd), .en(r30we_t), .Q(r30q_t), .clk(clk));  // open: clr
  Register_part #(.width(32)) x3 (.D(rd), .en(r3we_t), .Q(r3q_t), .clk(clk));  // open: clr
  Register_part #(.width(32)) x7 (.D(rd), .en(r7we_t), .Q(r7q_t), .clk(clk));  // open: clr
  Register_part #(.width(32)) x11 (.D(rd), .en(r11we_t), .Q(r11q_t), .clk(clk));  // open: clr
  Register_part #(.width(32)) x15 (.D(rd), .en(r15we_t), .Q(r15q_t), .clk(clk));  // open: clr
  Register_part #(.width(32)) x19 (.D(rd), .en(r19we_t), .Q(r19q_t), .clk(clk));  // open: clr
  Register_part #(.width(32)) x23 (.D(rd), .en(r23we_t), .Q(r23q_t), .clk(clk));  // open: clr
  Register_part #(.width(32)) x27 (.D(rd), .en(r27we_t), .Q(r27q_t), .clk(clk));  // open: clr
  Register_part #(.width(32)) x31 (.D(rd), .en(r31we_t), .Q(r31q_t), .clk(clk));  // open: clr

  // Other names for the same wires on the sheet: clk_t = clk; rd_t[31:0] = rd; rdi_t[4:0] = rdi; rs1_t[31:0] = rs1;
  //   rs2_t[31:0] = rs2; rsi1_t[4:0] = rsi1; rsi2_t[4:0] = rsi2; we_t = we

  // Notes on the sheet:
  //   ADD rd, rsi1, rsi2
  //   Register File
endmodule

module ALU (
  input  [31:0] dataA,
  input  [31:0] dataB,
  input  [3:0] Sel,
  output [31:0] dataD
);

  wire comparator_1_lt, comparator_2_lt;
  wire [31:0] addOut, andOut, orOut, sllOut, slraOut, slrOut, sltOut, subOut, xorOut;

  Multiplexer #(.select(4), .width(32)) multiplexer_1 (
    .in0(addOut), .in1(sllOut), .in2(sltOut), .in3(sltOut), .in4(xorOut), .in5(slrOut), .in6(orOut),
    .in7(andOut), .in8(subOut), .in13(slraOut), .out(dataD), .sel(Sel));  // open: in9, in10, in11, in12, in14, in15, en
  Adder #(.width(32)) adder_1 (.a(dataA), .b(dataB), .out(addOut));  // open: cin, cout
  Subtractor #(.width(32)) subtractor_1 (.a(dataA), .b(dataB), .out(subOut));  // open: bin, bout
  Shifter #(.width(32)) shifter_1 (.in(dataA), .\dist (dataB[4:0]), .out(sllOut));
  Comparator #(.width(32)) comparator_1 (.a(dataA), .b(dataB), .lt(comparator_1_lt));  // open: gt, eq
  Comparator #(.width(32), .mode("unsigned")) comparator_2 (
    .a(dataA), .b(dataB), .lt(comparator_2_lt));  // open: gt, eq
  assign xorOut = dataA ^ dataB;  // XOR_Gate xor_1, 32 bits wide
  Shifter #(.width(32), .shift("lr")) shifter_2 (.in(dataA), .\dist (dataB[4:0]), .out(slrOut));
  Shifter #(.width(32), .shift("ar")) shifter_3 (.in(dataA), .\dist (dataB[4:0]), .out(slraOut));
  assign orOut = dataA | dataB;  // OR_Gate or_1, 32 bits wide
  assign andOut = dataA & dataB;  // AND_Gate and_1, 32 bits wide
  assign sltOut = {{31{1'b0}}, comparator_1_lt};  // Bit_Extender bit_extender_1
  assign sltOut = {{31{1'b0}}, comparator_2_lt};  // Bit_Extender bit_extender_2

  // Other names for the same wires on the sheet: dataA_t[31:0] = dataA; dataB_t[31:0] = dataB;
  //   dataBL5_t[4:0] = dataB[4:0]; dataD_t[31:0] = dataD; Sel_t[3:0] = Sel; sltuOut[31:0] = sltOut

  // Notes on the sheet:
  //    Sel	              Operation
  //   RV32I ALU Operations
  //   0000	             add – Sumation
  //   1000	             sub – Subtraction
  //   0001	              sll – Shift Left Logical
  //   0010	             slt – Set Less Than
  //   0011	            sltu – Set Less Than Unsigned
  //   0100	             xor – eXclusive OR
  //   0101              	srl – Shift Right Logical
  //   1101             sra – Shift Right Arithmetic
  //   0110          	  or – logical OR
  //   0111	            and – logical AND
endmodule

module Brancher (
  input  [31:0] dataA,
  input  [31:0] dataB,
  input  brUn,
  output brLt,
  output beEq
);

  wire comparator_1_lt, comparator_2_lt;

  Comparator #(.width(32)) comparator_1 (.a(dataA), .b(dataB), .eq(beEq), .lt(comparator_1_lt));  // open: gt
  Comparator #(.width(32), .mode("unsigned")) comparator_2 (
    .a(dataA), .b(dataB), .lt(comparator_2_lt));  // open: gt, eq
  Multiplexer multiplexer_1 (.in0(comparator_1_lt), .in1(comparator_2_lt), .out(brLt), .sel(brUn));  // open: en

  // Other names for the same wires on the sheet: beEq_t = beEq; brLt_t = brLt; brUn_t = brUn; dataA_t[31:0] = dataA;
  //   dataB_t[31:0] = dataB
endmodule

module ImmediateGen (
  input  [31:0] Ins,
  input  [2:0] sel,
  output [31:0] imm31_0
);

  wire [3:0] bsplitter_1_imm4_1;
  wire [4:0] ssplitter_1_imm4_0;
  wire [5:0] bsplitter_1_imm10_5;
  wire [6:0] ssplitter_1_imm11_5;
  wire [7:0] jsplitter_1_imm19_12;
  wire [9:0] jsplitter_1_imm10_1;
  wire [11:0] isplitter_1_imm11_0;
  wire [12:11] bsplitter_1_imm11;
  wire [20:11] jsplitter_1_imm11;
  wire [31:0] BOut_t, IOut_t, JOut_t, SOut_t;
  wire [31:12] UOut_t;

  Multiplexer #(.select(3), .width(32)) multiplexer_1 (
    .in0(IOut_t), .in1(SOut_t), .in2(BOut_t), .in3(JOut_t), .in4({UOut_t, {12{1'b0}}}), .out(imm31_0),
    .sel(sel));  // open: in5, in6, in7, en
  ISplitter isplitter_1 (.Ins(Ins), .imm11_0(isplitter_1_imm11_0));  // open: opcode, rd, funct3, rs1
  SSplitter ssplitter_1 (
    .Ins(Ins), .imm4_0(ssplitter_1_imm4_0), .imm11_5(ssplitter_1_imm11_5));  // open: opcode, funct3, rs1, rs2
  BSplitter bsplitter_1 (
    .ins(Ins), .imm11(bsplitter_1_imm11[11]), .imm4_1(bsplitter_1_imm4_1), .imm10_5(bsplitter_1_imm10_5),
    .imm12(bsplitter_1_imm11[12]));  // open: opcode, funct3, rs1, rs2
  JSplitter jsplitter_1 (
    .Ins(Ins), .imm19_12(jsplitter_1_imm19_12), .imm11(jsplitter_1_imm11[11]), .imm10_1(jsplitter_1_imm10_1),
    .imm20(jsplitter_1_imm11[20]));  // open: opcode, rd
  USplitter usplitter_1 (.Ins(Ins), .imm31_12(UOut_t));  // open: opcode, rd
  assign IOut_t = {{20{isplitter_1_imm11_0[11]}}, isplitter_1_imm11_0};  // Bit_Extender bit_extender_1
  assign SOut_t = {{20{ssplitter_1_imm11_5[6]}}, {ssplitter_1_imm11_5, ssplitter_1_imm4_0}};  // Bit_Extender bit_extender_2
  assign BOut_t = {{19{bsplitter_1_imm11[12]}}, {bsplitter_1_imm11, bsplitter_1_imm10_5, bsplitter_1_imm4_1, 1'b0}};  // Bit_Extender bit_extender_3
  assign JOut_t = {{11{jsplitter_1_imm11[20]}}, {jsplitter_1_imm11[20], jsplitter_1_imm19_12, jsplitter_1_imm11[11], jsplitter_1_imm10_1, 1'b0}};  // Bit_Extender bit_extender_4

  // Other names for the same wires on the sheet: imm31_0_t[31:0] = imm31_0; Ins_t[31:0] = Ins; sel_t[2:0] = sel
endmodule

module ISplitter (
  input  [31:0] Ins,
  output [6:0] opcode,
  output [4:0] rd,
  output [2:0] funct3,
  output [4:0] rs1,
  output [11:0] imm11_0
);


  assign funct3 = Ins[14:12];
  assign imm11_0 = Ins[31:20];
  assign opcode = Ins[6:0];
  assign rd = Ins[11:7];
  assign rs1 = Ins[19:15];

  // Notes on the sheet:
  //   Immediate Variant I -Type
  //   Immediate Arithmetic/Logical/Shift Operations
  //   I - Types are also used in Load and Compare ops
endmodule

module SSplitter (
  input  [31:0] Ins,
  output [6:0] opcode,
  output [4:0] imm4_0,
  output [2:0] funct3,
  output [4:0] rs1,
  output [4:0] rs2,
  output [6:0] imm11_5
);


  assign funct3 = Ins[14:12];
  assign imm4_0 = Ins[11:7];
  assign imm11_5 = Ins[31:25];
  assign opcode = Ins[6:0];
  assign rs1 = Ins[19:15];
  assign rs2 = Ins[24:20];

  // Notes on the sheet:
  //   Immediate Variant S - Type
  //   Store Operations
endmodule

module BSplitter (
  input  [31:0] ins,
  output [6:0] opcode,
  output imm11,
  output [3:0] imm4_1,
  output [2:0] funct3,
  output [4:0] rs1,
  output [4:0] rs2,
  output [5:0] imm10_5,
  output imm12
);


  assign funct3 = ins[14:12];
  assign imm4_1 = ins[11:8];
  assign imm10_5 = ins[30:25];
  assign imm11 = ins[7];
  assign imm12 = ins[31];
  assign opcode = ins[6:0];
  assign rs1 = ins[19:15];
  assign rs2 = ins[24:20];

  // Notes on the sheet:
  //   Immediate Variant B - Type
  //   Branch Operations
endmodule

module USplitter (
  input  [31:0] Ins,
  output [6:0] opcode,
  output [4:0] rd,
  output [19:0] imm31_12
);


  assign imm31_12 = Ins[31:12];
  assign opcode = Ins[6:0];
  assign rd = Ins[11:7];

  // Notes on the sheet:
  //   Immediate Variant U - Type
  //   Upper Immediate Operations
endmodule

module JSplitter (
  input  [31:0] Ins,
  output [6:0] opcode,
  output [4:0] rd,
  output [7:0] imm19_12,
  output imm11,
  output [9:0] imm10_1,
  output imm20
);


  assign imm10_1 = Ins[30:21];
  assign imm11 = Ins[20];
  assign imm19_12 = Ins[19:12];
  assign imm20 = Ins[31];
  assign opcode = Ins[6:0];
  assign rd = Ins[11:7];

  // Notes on the sheet:
  //   Immediate Variant J - Type
  //   Jump Operations
endmodule

module RSplitter (
  input  [31:0] Ins,
  output [6:0] opcode,
  output [4:0] rd,
  output [2:0] funct3,
  output [4:0] rs1,
  output [4:0] rs2,
  output [6:0] funct7
);


  assign funct3 = Ins[14:12];
  assign funct7 = Ins[31:25];
  assign opcode = Ins[6:0];
  assign rd = Ins[11:7];
  assign rs1 = Ins[19:15];
  assign rs2 = Ins[24:20];
endmodule

module ALUCTL (
  input  [31:0] rs2,
  input  [31:0] imm31_0,
  input  bsel,
  output [31:0] dataB
);

  Multiplexer #(.width(32)) multiplexer_1 (.in0(rs2), .in1(imm31_0), .out(dataB), .sel(bsel));  // open: en
endmodule

module LoadByte (
  input  [31:0] A,
  input  [31:0] lw,
  output [31:0] lb,
  output [31:0] lbu,
  output [31:0] out_5,
  output [31:0] out_6,
  output [31:0] out_7
);

  wire [4:0] bitselector_1_out;
  wire [7:0] bitselector_2_out;
  wire [31:0] shifter_2_out;

  assign out_5 = A & 32'h3;  // AND_Gate and_1, 32 bits wide
  Subtractor #(.width(32)) subtractor_1 (.a(32'h3), .b(out_5), .out(out_6));  // open: bin, bout
  Shifter #(.width(32)) shifter_1 (.in(out_6), .\dist (5'b00011), .out(out_7));
  BitSelector #(.width(32), .group(5)) bitselector_1 (.in(out_7), .out(bitselector_1_out), .sel(3'b000));
  Shifter #(.width(32), .shift("lr")) shifter_2 (.in(lw), .\dist (bitselector_1_out), .out(shifter_2_out));
  assign lbu = 32'hff & shifter_2_out;  // AND_Gate and_2, 32 bits wide
  BitSelector #(.width(32), .group(8)) bitselector_2 (.in(shifter_2_out), .out(bitselector_2_out), .sel(2'b00));
  assign lb = {{24{bitselector_2_out[7]}}, bitselector_2_out};  // Bit_Extender bit_extender_1

  // Other names for the same wires on the sheet: A_t[31:0] = A; lb_t[31:0] = lb; lbu_t[31:0] = lbu; lw_t[31:0] = lw
endmodule

module LoadHalfWord (
  input  [31:0] A,
  input  [31:0] lw,
  output [31:0] lh,
  output [31:0] lhu
);

  wire bitselector_1_out, not_1_out;
  wire [15:0] bitselector_2_out;

  BitSelector #(.width(32)) bitselector_1 (.in(A), .out(bitselector_1_out), .sel(5'b00001));
  BitSelector #(.width(32), .group(16)) bitselector_2 (.in(lw), .out(bitselector_2_out), .sel(not_1_out));
  not not_1 (not_1_out, bitselector_1_out);
  assign lh = {{16{bitselector_2_out[15]}}, bitselector_2_out};  // Bit_Extender bit_extender_1
  assign lhu = {{16{1'b0}}, bitselector_2_out};  // Bit_Extender bit_extender_2

  // Other names for the same wires on the sheet: A_t[31:0] = A; lh_t[31:0] = lh; lhu_t[31:0] = lhu; lw_t[31:0] = lw
endmodule

module LoadCtl (
  input  [31:0] A,
  input  [31:0] lw,
  input  [2:0] lsel,
  input  wbsel,
  output [31:0] out_5
);

  wire [31:0] loadbyte_1_lb, loadbyte_1_lbu, loadbyte_1_out_5, loadhalfword_1_lh, loadhalfword_1_lhu,
       multiplexer_1_out;

  LoadByte loadbyte_1 (
    .A(A), .lw(lw), .lb(loadbyte_1_lb), .lbu(loadbyte_1_lbu), .out_5(loadbyte_1_out_5),
    .out_7(loadbyte_1_out_5));  // open: out_6
  LoadHalfWord loadhalfword_1 (.A(A), .lw(lw), .lh(loadhalfword_1_lh), .lhu(loadhalfword_1_lhu));
  Multiplexer #(.select(3), .width(32)) multiplexer_1 (
    .in0(loadbyte_1_lb), .in1(loadhalfword_1_lh), .in2(lw), .in4(loadbyte_1_lbu), .in5(loadhalfword_1_lhu),
    .out(multiplexer_1_out), .sel(lsel));  // open: in3, in6, in7, en
  Multiplexer #(.width(32)) multiplexer_2 (.in0(multiplexer_1_out), .in1(A), .out(out_5), .sel(wbsel));  // open: en

  // Other names for the same wires on the sheet: A_t[31:0] = A; D_t[31:0] = out_5; lsel_t[2:0] = lsel;
  //   lw_t[31:0] = lw; wbsel_t = wbsel
endmodule
